// Logisim project lab1_part2.circ as structural Verilog: 1 circuit, main circuit main
module main (
  input  a,
  input  b,
  input  c,
  output f
);

  wire and_1_out, not_1_out, not_2_out, or_1_out;

  not not_1 (not_1_out, b);
  or or_1 (or_1_out, a, b);
  not not_2 (not_2_out, or_1_out);
  and and_1 (and_1_out, not_1_out, c);
  or or_2 (f, not_2_out, and_1_out);

  // Notes on the sheet:
  //   lab1_part2
  //   f=(a+b)'+cb'
endmodule
