// Logisim project Lab2Part3.circ as structural Verilog: 9 circuits, main circuit main
module main (
  input  SW3,
  input  SW2,
  input  SW1,
  input  SW0
);

  wire segment0_1_hex0, segment1_1_hex1, segment2_1_hex2, segment3_1_hex3, segment4_1_hex4, segment5_1_hex5,
       segment6_1_hex6;

  Segment0 segment0_1 (.SW3(SW3), .SW2(SW2), .SW1(SW1), .SW0(SW0), .HEX0(segment0_1_hex0));
  Segment1 segment1_1 (.SW3(SW3), .SW2(SW2), .SW1(SW1), .SW0(SW0), .HEX1(segment1_1_hex1));
  Segment2 segment2_1 (.SW3(SW3), .SW2(SW2), .SW1(SW1), .SW0(SW0), .HEX2(segment2_1_hex2));
  _7_Segment_Display u_7_segment_display_1 (
    .g(segment6_1_hex6), .f(segment5_1_hex5), .a(segment0_1_hex0), .b(segment1_1_hex1), .e(segment4_1_hex4),
    .d(segment3_1_hex3), .c(segment2_1_hex2));  // open: dp
  Segment3 segment3_1 (.SW3(SW3), .SW2(SW2), .SW1(SW1), .SW0(SW0), .HEX3(segment3_1_hex3));
  Segment4 segment4_1 (.SW3(SW3), .SW2(SW2), .SW1(SW1), .SW0(SW0), .HEX4(segment4_1_hex4));
  Segment5 segment5_1 (.SW3(SW3), .SW2(SW2), .SW1(SW1), .SW0(SW0), .HEX5(segment5_1_hex5));
  Segment6 segment6_1 (.SW3(SW3), .SW2(SW2), .SW1(SW1), .SW0(SW0), .HEX6(segment6_1_hex6));
endmodule

module SegmentExample (
  input  SW3,
  input  SW2,
  input  SW1,
  input  SW0,
  output HEX
);

  wire not_1_out, not_2_out, not_3_out, not_4_out;

  not not_1 (not_1_out, SW3);
  not not_2 (not_2_out, SW2);
  not not_3 (not_3_out, SW1);
  not not_4 (not_4_out, SW0);
endmodule

module Segment0 (
  input  SW3,
  input  SW2,
  input  SW1,
  input  SW0,
  output HEX0
);

  wire and_1_out, and_2_out, and_3_out, and_4_out, and_5_out, and_6_out, not_1_out, not_2_out, not_3_out,
       not_4_out;

  not not_1 (not_1_out, SW3);
  not not_2 (not_2_out, SW2);
  not not_3 (not_3_out, SW1);
  not not_4 (not_4_out, SW0);
  and and_1 (and_1_out, SW1, not_1_out);
  and and_2 (and_2_out, not_4_out, SW3);
  and and_3 (and_3_out, not_4_out, not_2_out);
  and and_4 (and_4_out, SW0, SW2, not_1_out);
  and and_5 (and_5_out, SW1, SW2);
  and and_6 (and_6_out, not_3_out, not_2_out, SW3);
  or or_1 (HEX0, and_6_out, and_4_out, and_5_out, and_1_out, and_2_out, and_3_out);
endmodule

module Segment1 (
  input  SW3,
  input  SW2,
  input  SW1,
  input  SW0,
  output HEX1
);

  wire and_1_out, and_2_out, and_3_out, and_4_out, not_1_out, not_2_out, not_3_out, not_4_out, xnor_1_out;

  not not_1 (not_1_out, SW3);
  not not_2 (not_2_out, SW2);
  not not_3 (not_3_out, SW1);
  not not_4 (not_4_out, SW0);
  and and_1 (and_1_out, not_2_out, not_1_out);
  xnor xnor_1 (xnor_1_out, SW0, SW1);
  and and_2 (and_2_out, not_4_out, not_2_out);
  and and_3 (and_3_out, SW0, not_3_out, SW3);
  and and_4 (and_4_out, xnor_1_out, not_1_out);
  or or_1 (HEX1, and_2_out, and_3_out, and_4_out, and_1_out);
endmodule

module Segment2 (
  input  SW3,
  input  SW2,
  input  SW1,
  input  SW0,
  output HEX2
);

  wire and_1_out, and_2_out, not_1_out, not_2_out, not_3_out, not_4_out, or_1_out, xor_1_out;

  not not_1 (not_1_out, SW3);
  not not_2 (not_2_out, SW2);
  not not_3 (not_3_out, SW1);
  not not_4 (not_4_out, SW0);
  or or_1 (or_1_out, not_3_out, not_1_out);
  and and_1 (and_1_out, not_3_out, not_1_out);
  xor xor_1 (xor_1_out, SW2, SW3);
  and and_2 (and_2_out, or_1_out, SW0);
  or or_2 (HEX2, and_2_out, and_1_out, xor_1_out);
endmodule

module Segment3 (
  input  SW3,
  input  SW2,
  input  SW1,
  input  SW0,
  output HEX3
);

  wire and_1_out, and_2_out, and_3_out, and_4_out, not_1_out, not_2_out, not_3_out, not_4_out, or_1_out,
       xor_1_out;

  not not_1 (not_1_out, SW3);
  not not_2 (not_2_out, SW2);
  not not_3 (not_3_out, SW1);
  not not_4 (not_4_out, SW0);
  or or_1 (or_1_out, not_4_out, SW1);
  and and_1 (and_1_out, not_3_out, SW3);
  xor xor_1 (xor_1_out, SW0, SW1);
  and and_2 (and_2_out, or_1_out, not_2_out, not_1_out);
  and and_3 (and_3_out, SW0, not_2_out, SW3);
  and and_4 (and_4_out, xor_1_out, SW2);
  or or_2 (HEX3, and_3_out, and_1_out, and_4_out, and_2_out);
endmodule

module Segment4 (
  input  SW3,
  input  SW2,
  input  SW1,
  input  SW0,
  output HEX4
);

  wire and_1_out, and_2_out, not_1_out, not_2_out, not_3_out, not_4_out, or_1_out, or_2_out;

  not not_1 (not_1_out, SW3);
  not not_2 (not_2_out, SW2);
  not not_3 (not_3_out, SW1);
  not not_4 (not_4_out, SW0);
  or or_1 (or_1_out, SW1, SW2);
  or or_2 (or_2_out, SW1, not_2_out);
  and and_1 (and_1_out, or_2_out, not_4_out);
  and and_2 (and_2_out, or_1_out, SW3);
  or or_3 (HEX4, and_2_out, and_1_out);
endmodule

module Segment5 (
  input  SW3,
  input  SW2,
  input  SW1,
  input  SW0,
  output HEX5
);

  wire and_1_out, and_2_out, and_3_out, not_1_out, not_2_out, not_3_out, not_4_out, or_1_out, or_2_out;

  not not_1 (not_1_out, SW3);
  not not_2 (not_2_out, SW2);
  not not_3 (not_3_out, SW1);
  not not_4 (not_4_out, SW0);
  or or_1 (or_1_out, not_3_out, SW2);
  and and_1 (and_1_out, not_3_out, SW2, not_1_out);
  or or_2 (or_2_out, SW1, not_2_out);
  and and_2 (and_2_out, or_2_out, SW3);
  and and_3 (and_3_out, or_1_out, not_4_out);
  or or_3 (HEX5, and_1_out, and_2_out, and_3_out);
endmodule

module Segment6 (
  input  SW3,
  input  SW2,
  input  SW1,
  input  SW0,
  output HEX6
);

  wire and_1_out, and_2_out, and_3_out, not_1_out, not_2_out, not_3_out, not_4_out, or_1_out, or_2_out;

  not not_1 (not_1_out, SW3);
  not not_2 (not_2_out, SW2);
  not not_3 (not_3_out, SW1);
  not not_4 (not_4_out, SW0);
  or or_1 (or_1_out, not_4_out, not_2_out);
  and and_1 (and_1_out, not_3_out, SW2, not_1_out);
  or or_2 (or_2_out, SW0, SW1, not_2_out);
  and and_2 (and_2_out, or_1_out, SW1);
  and and_3 (and_3_out, or_2_out, SW3);
  or or_3 (HEX6, and_3_out, and_2_out, and_1_out);
endmodule
