// Logisim project Lab3Part1.circ as structural Verilog: 1 circuit, main circuit main
module main (
  input  [6:0] SW,
  input  [2:0] SB,
  output LEDR
);

  Multiplexer #(.enable("false"), .select(3)) multiplexer_1 (
    .in0(SW[6]), .in1(SW[5]), .in2(SW[4]), .in3(SW[3]), .in4(SW[2]), .in5(SW[1]), .in6(SW[0]), .out(LEDR),
    .sel(SB));  // open: in7
endmodule
