// Logisim project Lab3Part2.circ as structural Verilog: 3 circuits, main circuit main
module main (
  input  [3:0] A,
  input  C_in,
  input  [3:0] B,
  output C_out,
  output [3:0] LEDR
);

  ripple_carry_adder ripple_carry_adder_1 (.A(A), .C_in(C_in), .B(B), .C_out(C_out), .LEDR(LEDR));
endmodule

module full_adder (
  input  ci,
  input  a,
  input  b,
  output s,
  output co
);

  wire xor_1_out;

  xor xor_1 (xor_1_out, a, b);
  Multiplexer #(.enable("false")) multiplexer_1 (.in0(b), .in1(ci), .out(co), .sel(xor_1_out));
  xor xor_2 (s, ci, xor_1_out);
endmodule

module ripple_carry_adder (
  input  [3:0] A,
  input  C_in,
  input  [3:0] B,
  output C_out,
  output [3:0] LEDR
);

  wire full_adder_2_co, full_adder_3_co, full_adder_4_co;

  full_adder full_adder_1 (.ci(full_adder_2_co), .a(A[3]), .b(B[3]), .s(LEDR[3]), .co(C_out));
  full_adder full_adder_2 (.ci(full_adder_3_co), .a(A[2]), .b(B[2]), .s(LEDR[2]), .co(full_adder_2_co));
  full_adder full_adder_3 (.ci(full_adder_4_co), .a(A[1]), .b(B[1]), .s(LEDR[1]), .co(full_adder_3_co));
  full_adder full_adder_4 (.ci(C_in), .a(A[0]), .b(B[0]), .s(LEDR[0]), .co(full_adder_4_co));
endmodule
