// Logisim project Lab4Part2.circ as structural Verilog: 21 circuits, main circuit main
module main (
  input  [3:0] A,
  input  [2:0] ALUfunction,
  input  WE,
  input  Clk,
  output [7:0] ALUout
);

  wire haxdecoder_1_hex0, haxdecoder_1_hex1, haxdecoder_1_hex2, haxdecoder_1_hex3, haxdecoder_1_hex4,
       haxdecoder_1_hex5, haxdecoder_1_hex6, haxdecoder_2_hex0, haxdecoder_2_hex1, haxdecoder_2_hex2,
       haxdecoder_2_hex3, haxdecoder_2_hex4, haxdecoder_2_hex5, haxdecoder_2_hex6, haxdecoder_3_hex0,
       haxdecoder_3_hex1, haxdecoder_3_hex2, haxdecoder_3_hex3, haxdecoder_3_hex4, haxdecoder_3_hex5,
       haxdecoder_3_hex6, haxdecoder_4_hex0, haxdecoder_4_hex1, haxdecoder_4_hex2, haxdecoder_4_hex3,
       haxdecoder_4_hex4, haxdecoder_4_hex5, haxdecoder_4_hex6;
  wire [3:0] bit_extender_1_out;
  wire [7:0] alu_1_aluout;

  Bit_Extender #(.out_width(4), .\type ("zero")) bit_extender_1 (.in(ALUout), .out(bit_extender_1_out));
  ALU alu_1 (.A(A), .B(bit_extender_1_out), .ALUfunction(ALUfunction), .ALUout(alu_1_aluout));
  HaxDecoder haxdecoder_1 (
    .SW3(A[3]), .SW2(A[2]), .SW1(A[1]), .SW0(A[0]), .HEX0(haxdecoder_1_hex0), .HEX1(haxdecoder_1_hex1),
    .HEX2(haxdecoder_1_hex2), .HEX3(haxdecoder_1_hex3), .HEX4(haxdecoder_1_hex4), .HEX5(haxdecoder_1_hex5),
    .HEX6(haxdecoder_1_hex6));
  HaxDecoder haxdecoder_2 (
    .SW3(bit_extender_1_out[3]), .SW2(bit_extender_1_out[2]), .SW1(bit_extender_1_out[1]),
    .SW0(bit_extender_1_out[0]), .HEX0(haxdecoder_2_hex0), .HEX1(haxdecoder_2_hex1),
    .HEX2(haxdecoder_2_hex2), .HEX3(haxdecoder_2_hex3), .HEX4(haxdecoder_2_hex4), .HEX5(haxdecoder_2_hex5),
    .HEX6(haxdecoder_2_hex6));
  Register register_1 (.D(alu_1_aluout), .en(WE), .clk(Clk), .Q(ALUout));  // open: clr
  _7_Segment_Display u_7_segment_display_1 (
    .g(haxdecoder_1_hex6), .f(haxdecoder_1_hex5), .a(haxdecoder_1_hex0), .b(haxdecoder_1_hex1),
    .e(haxdecoder_1_hex4), .d(haxdecoder_1_hex3), .c(haxdecoder_1_hex2));  // open: dp
  _7_Segment_Display u_7_segment_display_2 (
    .g(haxdecoder_2_hex6), .f(haxdecoder_2_hex5), .a(haxdecoder_2_hex0), .b(haxdecoder_2_hex1),
    .e(haxdecoder_2_hex4), .d(haxdecoder_2_hex3), .c(haxdecoder_2_hex2));  // open: dp
  LED led_1 (.in(ALUout[7]));
  LED led_2 (.in(ALUout[6]));
  LED led_3 (.in(ALUout[5]));
  LED led_4 (.in(ALUout[4]));
  LED led_5 (.in(ALUout[3]));
  HaxDecoder haxdecoder_3 (
    .SW3(ALUout[3]), .SW2(ALUout[2]), .SW1(ALUout[1]), .SW0(ALUout[0]), .HEX0(haxdecoder_3_hex0),
    .HEX1(haxdecoder_3_hex1), .HEX2(haxdecoder_3_hex2), .HEX3(haxdecoder_3_hex3), .HEX4(haxdecoder_3_hex4),
    .HEX5(haxdecoder_3_hex5), .HEX6(haxdecoder_3_hex6));
  HaxDecoder haxdecoder_4 (
    .SW3(ALUout[7]), .SW2(ALUout[6]), .SW1(ALUout[5]), .SW0(ALUout[4]), .HEX0(haxdecoder_4_hex0),
    .HEX1(haxdecoder_4_hex1), .HEX2(haxdecoder_4_hex2), .HEX3(haxdecoder_4_hex3), .HEX4(haxdecoder_4_hex4),
    .HEX5(haxdecoder_4_hex5), .HEX6(haxdecoder_4_hex6));
  LED led_6 (.in(ALUout[2]));
  LED led_7 (.in(ALUout[1]));
  LED led_8 (.in(ALUout[0]));
  _7_Segment_Display u_7_segment_display_3 (
    .g(haxdecoder_3_hex6), .f(haxdecoder_3_hex5), .a(haxdecoder_3_hex0), .b(haxdecoder_3_hex1),
    .e(haxdecoder_3_hex4), .d(haxdecoder_3_hex3), .c(haxdecoder_3_hex2));  // open: dp
  _7_Segment_Display u_7_segment_display_4 (
    .g(haxdecoder_4_hex6), .f(haxdecoder_4_hex5), .a(haxdecoder_4_hex0), .b(haxdecoder_4_hex1),
    .e(haxdecoder_4_hex4), .d(haxdecoder_4_hex3), .c(haxdecoder_4_hex2));  // open: dp

  // Notes on the sheet:
  //   A
  //   A
endmodule

module HaxDecoder (
  input  SW3,
  input  SW2,
  input  SW1,
  input  SW0,
  output HEX0,
  output HEX1,
  output HEX2,
  output HEX3,
  output HEX4,
  output HEX5,
  output HEX6
);

  Segment0 segment0_1 (.SW3(SW3), .SW2(SW2), .SW1(SW1), .SW0(SW0), .HEX0(HEX0));
  Segment1 segment1_1 (.SW3(SW3), .SW2(SW2), .SW1(SW1), .SW0(SW0), .HEX1(HEX1));
  Segment2 segment2_1 (.SW3(SW3), .SW2(SW2), .SW1(SW1), .SW0(SW0), .HEX2(HEX2));
  Segment3 segment3_1 (.SW3(SW3), .SW2(SW2), .SW1(SW1), .SW0(SW0), .HEX3(HEX3));
  Segment4 segment4_1 (.SW3(SW3), .SW2(SW2), .SW1(SW1), .SW0(SW0), .HEX4(HEX4));
  Segment5 segment5_1 (.SW3(SW3), .SW2(SW2), .SW1(SW1), .SW0(SW0), .HEX5(HEX5));
  Segment6 segment6_1 (.SW3(SW3), .SW2(SW2), .SW1(SW1), .SW0(SW0), .HEX6(HEX6));
endmodule

module ALU (
  input  [3:0] A,
  input  [3:0] B,
  input  [2:0] ALUfunction,
  output [7:0] ALUout
);

  wire haxdecoder_1_hex0, haxdecoder_1_hex1, haxdecoder_1_hex2, haxdecoder_1_hex3, haxdecoder_1_hex4,
       haxdecoder_1_hex5, haxdecoder_1_hex6, haxdecoder_2_hex0, haxdecoder_2_hex1, haxdecoder_2_hex2,
       haxdecoder_2_hex3, haxdecoder_2_hex4, haxdecoder_2_hex5, haxdecoder_2_hex6, haxdecoder_3_hex0,
       haxdecoder_3_hex1, haxdecoder_3_hex2, haxdecoder_3_hex3, haxdecoder_3_hex4, haxdecoder_3_hex5,
       haxdecoder_3_hex6, haxdecoder_4_hex0, haxdecoder_4_hex1, haxdecoder_4_hex2, haxdecoder_4_hex3,
       haxdecoder_4_hex4, haxdecoder_4_hex5, haxdecoder_4_hex6;
  wire [7:0] function0_1_aluout, function1_1_aluout, function2_1_aluout, function3_1_aluout,
       function4_1_aluout, function5_1_aluout, function6_1_aluout, function7_1_aluout;

  HaxDecoder haxdecoder_1 (
    .SW3(B[3]), .SW2(B[2]), .SW1(B[1]), .SW0(B[0]), .HEX0(haxdecoder_1_hex0), .HEX1(haxdecoder_1_hex1),
    .HEX2(haxdecoder_1_hex2), .HEX3(haxdecoder_1_hex3), .HEX4(haxdecoder_1_hex4), .HEX5(haxdecoder_1_hex5),
    .HEX6(haxdecoder_1_hex6));
  HaxDecoder haxdecoder_2 (
    .SW3(A[3]), .SW2(A[2]), .SW1(A[1]), .SW0(A[0]), .HEX0(haxdecoder_2_hex0), .HEX1(haxdecoder_2_hex1),
    .HEX2(haxdecoder_2_hex2), .HEX3(haxdecoder_2_hex3), .HEX4(haxdecoder_2_hex4), .HEX5(haxdecoder_2_hex5),
    .HEX6(haxdecoder_2_hex6));
  function0 function0_1 (.A(A), .ALUout(function0_1_aluout));
  function1 function1_1 (.A(A), .B(B), .ALUout(function1_1_aluout));
  function2 function2_1 (.A(A), .B(B), .ALUout(function2_1_aluout));
  function3 function3_1 (.A(A), .B(B), .ALUout(function3_1_aluout));
  function4 function4_1 (.A(A), .B(B), .ALUout(function4_1_aluout));
  function5 function5_1 (.B(B), .A(A), .ALUout(function5_1_aluout));
  function6 function6_1 (.B(B), .A(A), .ALUout(function6_1_aluout));
  function7 function7_1 (.A(A), .B(B), .ALUout(function7_1_aluout));
  Multiplexer #(.enable("false"), .select(3), .width(8)) multiplexer_1 (
    .in0(function0_1_aluout), .in1(function1_1_aluout), .in2(function2_1_aluout), .in3(function3_1_aluout),
    .in4(function4_1_aluout), .in5(function5_1_aluout), .in6(function6_1_aluout), .in7(function7_1_aluout),
    .out(ALUout), .sel(ALUfunction));
  _7_Segment_Display u_7_segment_display_1 (
    .g(haxdecoder_1_hex6), .f(haxdecoder_1_hex5), .a(haxdecoder_1_hex0), .b(haxdecoder_1_hex1),
    .e(haxdecoder_1_hex4), .d(haxdecoder_1_hex3), .c(haxdecoder_1_hex2));  // open: dp
  _7_Segment_Display u_7_segment_display_2 (
    .g(haxdecoder_2_hex6), .f(haxdecoder_2_hex5), .a(haxdecoder_2_hex0), .b(haxdecoder_2_hex1),
    .e(haxdecoder_2_hex4), .d(haxdecoder_2_hex3), .c(haxdecoder_2_hex2));  // open: dp
  LED led_1 (.in(ALUout[6]));
  LED led_2 (.in(ALUout[5]));
  LED led_3 (.in(ALUout[7]));
  LED led_4 (.in(ALUout[4]));
  LED led_5 (.in(ALUout[3]));
  LED led_6 (.in(ALUout[2]));
  LED led_7 (.in(ALUout[1]));
  HaxDecoder haxdecoder_3 (
    .SW3(ALUout[3]), .SW2(ALUout[2]), .SW1(ALUout[1]), .SW0(ALUout[0]), .HEX0(haxdecoder_3_hex0),
    .HEX1(haxdecoder_3_hex1), .HEX2(haxdecoder_3_hex2), .HEX3(haxdecoder_3_hex3), .HEX4(haxdecoder_3_hex4),
    .HEX5(haxdecoder_3_hex5), .HEX6(haxdecoder_3_hex6));
  HaxDecoder haxdecoder_4 (
    .SW3(ALUout[7]), .SW2(ALUout[6]), .SW1(ALUout[5]), .SW0(ALUout[4]), .HEX0(haxdecoder_4_hex0),
    .HEX1(haxdecoder_4_hex1), .HEX2(haxdecoder_4_hex2), .HEX3(haxdecoder_4_hex3), .HEX4(haxdecoder_4_hex4),
    .HEX5(haxdecoder_4_hex5), .HEX6(haxdecoder_4_hex6));
  LED led_8 (.in(ALUout[0]));
  _7_Segment_Display u_7_segment_display_3 (
    .g(haxdecoder_3_hex6), .f(haxdecoder_3_hex5), .a(haxdecoder_3_hex0), .b(haxdecoder_3_hex1),
    .e(haxdecoder_3_hex4), .d(haxdecoder_3_hex3), .c(haxdecoder_3_hex2));  // open: dp
  _7_Segment_Display u_7_segment_display_4 (
    .g(haxdecoder_4_hex6), .f(haxdecoder_4_hex5), .a(haxdecoder_4_hex0), .b(haxdecoder_4_hex1),
    .e(haxdecoder_4_hex4), .d(haxdecoder_4_hex3), .c(haxdecoder_4_hex2));  // open: dp

  // Notes on the sheet:
  //   B
  //   A
endmodule

module ripple_carry_adder (
  input  [3:0] A,
  input  C_in,
  input  [3:0] B,
  output C_out,
  output [3:0] LEDR
);

  wire full_adder_2_co, full_adder_3_co, full_adder_4_co;

  full_adder full_adder_1 (.ci(full_adder_2_co), .a(A[3]), .b(B[3]), .s(LEDR[3]), .co(C_out));
  full_adder full_adder_2 (.ci(full_adder_3_co), .a(A[2]), .b(B[2]), .s(LEDR[2]), .co(full_adder_2_co));
  full_adder full_adder_3 (.ci(full_adder_4_co), .a(A[1]), .b(B[1]), .s(LEDR[1]), .co(full_adder_3_co));
  full_adder full_adder_4 (.ci(C_in), .a(A[0]), .b(B[0]), .s(LEDR[0]), .co(full_adder_4_co));
endmodule

module full_adder (
  input  ci,
  input  a,
  input  b,
  output s,
  output co
);

  wire xor_1_out;

  xor xor_1 (xor_1_out, a, b);
  Multiplexer #(.enable("false")) multiplexer_1 (.in0(b), .in1(ci), .out(co), .sel(xor_1_out));
  xor xor_2 (s, ci, xor_1_out);
endmodule

module SegmentExample (
  input  SW3,
  input  SW2,
  input  SW1,
  input  SW0,
  output HEX
);

  wire not_1_out, not_2_out, not_3_out, not_4_out;

  not not_1 (not_1_out, SW3);
  not not_2 (not_2_out, SW2);
  not not_3 (not_3_out, SW1);
  not not_4 (not_4_out, SW0);
endmodule

module Segment0 (
  input  SW3,
  input  SW2,
  input  SW1,
  input  SW0,
  output HEX0
);

  wire and_1_out, and_2_out, and_3_out, and_4_out, and_5_out, and_6_out, not_1_out, not_2_out, not_3_out,
       not_4_out;

  not not_1 (not_1_out, SW3);
  not not_2 (not_2_out, SW2);
  not not_3 (not_3_out, SW1);
  not not_4 (not_4_out, SW0);
  and and_1 (and_1_out, SW1, not_1_out);
  and and_2 (and_2_out, not_4_out, SW3);
  and and_3 (and_3_out, not_4_out, not_2_out);
  and and_4 (and_4_out, SW0, SW2, not_1_out);
  and and_5 (and_5_out, SW1, SW2);
  and and_6 (and_6_out, not_3_out, not_2_out, SW3);
  or or_1 (HEX0, and_6_out, and_4_out, and_5_out, and_1_out, and_2_out, and_3_out);
endmodule

module Segment1 (
  input  SW3,
  input  SW2,
  input  SW1,
  input  SW0,
  output HEX1
);

  wire and_1_out, and_2_out, and_3_out, and_4_out, not_1_out, not_2_out, not_3_out, not_4_out, xnor_1_out;

  not not_1 (not_1_out, SW3);
  not not_2 (not_2_out, SW2);
  not not_3 (not_3_out, SW1);
  not not_4 (not_4_out, SW0);
  and and_1 (and_1_out, not_2_out, not_1_out);
  xnor xnor_1 (xnor_1_out, SW0, SW1);
  and and_2 (and_2_out, not_4_out, not_2_out);
  and and_3 (and_3_out, SW0, not_3_out, SW3);
  and and_4 (and_4_out, xnor_1_out, not_1_out);
  or or_1 (HEX1, and_2_out, and_3_out, and_4_out, and_1_out);
endmodule

module Segment2 (
  input  SW3,
  input  SW2,
  input  SW1,
  input  SW0,
  output HEX2
);

  wire and_1_out, and_2_out, not_1_out, not_2_out, not_3_out, not_4_out, or_1_out, xor_1_out;

  not not_1 (not_1_out, SW3);
  not not_2 (not_2_out, SW2);
  not not_3 (not_3_out, SW1);
  not not_4 (not_4_out, SW0);
  or or_1 (or_1_out, not_3_out, not_1_out);
  and and_1 (and_1_out, not_3_out, not_1_out);
  xor xor_1 (xor_1_out, SW2, SW3);
  and and_2 (and_2_out, or_1_out, SW0);
  or or_2 (HEX2, and_2_out, and_1_out, xor_1_out);
endmodule

module Segment3 (
  input  SW3,
  input  SW2,
  input  SW1,
  input  SW0,
  output HEX3
);

  wire and_1_out, and_2_out, and_3_out, and_4_out, not_1_out, not_2_out, not_3_out, not_4_out, or_1_out,
       xor_1_out;

  not not_1 (not_1_out, SW3);
  not not_2 (not_2_out, SW2);
  not not_3 (not_3_out, SW1);
  not not_4 (not_4_out, SW0);
  or or_1 (or_1_out, not_4_out, SW1);
  and and_1 (and_1_out, not_3_out, SW3);
  xor xor_1 (xor_1_out, SW0, SW1);
  and and_2 (and_2_out, or_1_out, not_2_out, not_1_out);
  and and_3 (and_3_out, SW0, not_2_out, SW3);
  and and_4 (and_4_out, xor_1_out, SW2);
  or or_2 (HEX3, and_3_out, and_1_out, and_4_out, and_2_out);
endmodule

module Segment4 (
  input  SW3,
  input  SW2,
  input  SW1,
  input  SW0,
  output HEX4
);

  wire and_1_out, and_2_out, not_1_out, not_2_out, not_3_out, not_4_out, or_1_out, or_2_out;

  not not_1 (not_1_out, SW3);
  not not_2 (not_2_out, SW2);
  not not_3 (not_3_out, SW1);
  not not_4 (not_4_out, SW0);
  or or_1 (or_1_out, SW1, SW2);
  or or_2 (or_2_out, SW1, not_2_out);
  and and_1 (and_1_out, or_2_out, not_4_out);
  and and_2 (and_2_out, or_1_out, SW3);
  or or_3 (HEX4, and_2_out, and_1_out);
endmodule

module Segment5 (
  input  SW3,
  input  SW2,
  input  SW1,
  input  SW0,
  output HEX5
);

  wire and_1_out, and_2_out, and_3_out, not_1_out, not_2_out, not_3_out, not_4_out, or_1_out, or_2_out;

  not not_1 (not_1_out, SW3);
  not not_2 (not_2_out, SW2);
  not not_3 (not_3_out, SW1);
  not not_4 (not_4_out, SW0);
  or or_1 (or_1_out, not_3_out, SW2);
  and and_1 (and_1_out, not_3_out, SW2, not_1_out);
  or or_2 (or_2_out, SW1, not_2_out);
  and and_2 (and_2_out, or_2_out, SW3);
  and and_3 (and_3_out, or_1_out, not_4_out);
  or or_3 (HEX5, and_1_out, and_2_out, and_3_out);
endmodule

module Segment6 (
  input  SW3,
  input  SW2,
  input  SW1,
  input  SW0,
  output HEX6
);

  wire and_1_out, and_2_out, and_3_out, not_1_out, not_2_out, not_3_out, not_4_out, or_1_out, or_2_out;

  not not_1 (not_1_out, SW3);
  not not_2 (not_2_out, SW2);
  not not_3 (not_3_out, SW1);
  not not_4 (not_4_out, SW0);
  or or_1 (or_1_out, not_4_out, not_2_out);
  and and_1 (and_1_out, not_3_out, SW2, not_1_out);
  or or_2 (or_2_out, SW0, SW1, not_2_out);
  and and_2 (and_2_out, or_1_out, SW1);
  and and_3 (and_3_out, or_2_out, SW3);
  or or_3 (HEX6, and_3_out, and_2_out, and_1_out);
endmodule

module function0 (
  input  [3:0] A,
  output [7:0] ALUout
);

  wire ripple_carry_adder_1_c_out;

  ripple_carry_adder ripple_carry_adder_1 (
    .A(A), .C_in(1'b1), .B(4'b0000), .C_out(ripple_carry_adder_1_c_out), .LEDR(ALUout[3:0]));
  assign ALUout[7:4] = {{3{1'b0}}, ripple_carry_adder_1_c_out};  // Bit_Extender bit_extender_1
endmodule

module function1 (
  input  [3:0] A,
  input  [3:0] B,
  output [7:0] ALUout
);

  wire ripple_carry_adder_1_c_out;

  ripple_carry_adder ripple_carry_adder_1 (
    .A(A), .C_in(1'b0), .B(B), .C_out(ripple_carry_adder_1_c_out), .LEDR(ALUout[3:0]));
  assign ALUout[7:4] = {{3{1'b0}}, ripple_carry_adder_1_c_out};  // Bit_Extender bit_extender_1
endmodule

module function2 (
  input  [3:0] A,
  input  [3:0] B,
  output [7:0] ALUout
);

  wire adder_1_cout;

  Adder #(.width(4)) adder_1 (.a(A), .b(B), .out(ALUout[3:0]), .cin(1'b0), .cout(adder_1_cout));
  assign ALUout[7:4] = {{3{1'b0}}, adder_1_cout};  // Bit_Extender bit_extender_1
endmodule

module function3 (
  input  [3:0] A,
  input  [3:0] B,
  output [7:0] ALUout
);

  xor xor_1 (ALUout[0], A[0], B[0]);
  xor xor_2 (ALUout[1], B[1], A[1]);
  xor xor_3 (ALUout[2], B[2], A[2]);
  xor xor_4 (ALUout[3], B[3], A[3]);
  or or_1 (ALUout[4], B[0], A[0]);
  or or_2 (ALUout[5], B[1], A[1]);
  or or_3 (ALUout[6], B[2], A[2]);
  or or_4 (ALUout[7], B[3], A[3]);
endmodule

module function4 (
  input  [3:0] A,
  input  [3:0] B,
  output [7:0] ALUout
);

  wire or_1_out;

  or or_1 (or_1_out, A[0], A[1], A[2], A[3], B[0], B[1], B[2], B[3]);
  assign ALUout = {{7{1'b0}}, or_1_out};  // Bit_Extender bit_extender_1
endmodule

module function5 (
  input  [3:0] B,
  input  [3:0] A,
  output [7:0] ALUout
);

  wire [15:0] bit_extender_1_out, shifter_1_out;

  assign bit_extender_1_out = {{12{1'b0}}, B};  // Bit_Extender bit_extender_1
  Bit_Extender #(.in_width(16), .out_width(8), .\type ("zero")) bit_extender_2 (.in(shifter_1_out), .out(ALUout));
  Shifter #(.width(16)) shifter_1 (.in(bit_extender_1_out), .\dist (A), .out(shifter_1_out));
endmodule

module function6 (
  input  [3:0] B,
  input  [3:0] A,
  output [7:0] ALUout
);

  wire [15:0] bit_extender_1_out, shifter_1_out;

  assign bit_extender_1_out = {{12{1'b0}}, B};  // Bit_Extender bit_extender_1
  Bit_Extender #(.in_width(16), .out_width(8), .\type ("zero")) bit_extender_2 (.in(shifter_1_out), .out(ALUout));
  Shifter #(.shift("lr"), .width(16)) shifter_1 (.in(bit_extender_1_out), .\dist (A), .out(shifter_1_out));
endmodule

module function7 (
  input  [3:0] A,
  input  [3:0] B,
  output [7:0] ALUout
);

  Multiplier #(.width(4)) multiplier_1 (.a(A), .b(B), .out(ALUout[3:0]), .cin(4'b0000), .cout(ALUout[7:4]));
endmodule
