// Logisim project Lab4Part3.circ as structural Verilog
module ShifterBit (
  input  load_val,
  input  sin,
  input  shift,
  input  load_n,
  input  Clk,
  input  reset,
  output sout
);

  wire mux2to1_1_m, mux2to1_2_m;

  mux2to1 mux2to1_1 (.x(sout), .y(sin), .s(shift), .m(mux2to1_1_m));
  mux2to1 mux2to1_2 (.x(load_val), .y(mux2to1_1_m), .s(load_n), .m(mux2to1_2_m));
  D_Flip_Flop d_ff_1 (.D(mux2to1_2_m), .clk(Clk), .Q(sout), .reset(reset));  // open: Qn, preset
endmodule

module iShifter (
  input  [7:0] LoadVal,
  input  ShiftRight,
  input  load_n,
  input  Clk,
  input  reset,
  input  ASR,
  output [7:0] Q
);

  wire or_1_out;

  or or_1 (or_1_out, ASR, LoadVal[7]);
  ShifterBit shifterbit_1 (
    .load_val(LoadVal[7]), .sin(or_1_out), .shift(ShiftRight), .load_n(load_n), .Clk(Clk), .reset(reset),
    .sout(Q[7]));
  ShifterBit shifterbit_2 (
    .load_val(LoadVal[6]), .sin(Q[7]), .shift(ShiftRight), .load_n(load_n), .Clk(Clk), .reset(reset),
    .sout(Q[6]));
  ShifterBit shifterbit_3 (
    .load_val(LoadVal[5]), .sin(Q[6]), .shift(ShiftRight), .load_n(load_n), .Clk(Clk), .reset(reset),
    .sout(Q[5]));
  ShifterBit shifterbit_4 (
    .load_val(LoadVal[4]), .sin(Q[5]), .shift(ShiftRight), .load_n(load_n), .Clk(Clk), .reset(reset),
    .sout(Q[4]));
  ShifterBit shifterbit_5 (
    .load_val(LoadVal[3]), .sin(Q[4]), .shift(ShiftRight), .load_n(load_n), .Clk(Clk), .reset(reset),
    .sout(Q[3]));
  ShifterBit shifterbit_6 (
    .load_val(LoadVal[2]), .sin(Q[3]), .shift(ShiftRight), .load_n(load_n), .Clk(Clk), .reset(reset),
    .sout(Q[2]));
  ShifterBit shifterbit_7 (
    .load_val(LoadVal[1]), .sin(Q[2]), .shift(ShiftRight), .load_n(load_n), .Clk(Clk), .reset(reset),
    .sout(Q[1]));
  ShifterBit shifterbit_8 (
    .load_val(LoadVal[0]), .sin(Q[1]), .shift(ShiftRight), .load_n(load_n), .Clk(Clk), .reset(reset),
    .sout(Q[0]));
endmodule

module mux2to1 (
  input  x,
  input  y,
  input  s,
  output m
);

  Multiplexer #(.enable("false")) multiplexer_1 (.in0(x), .in1(y), .out(m), .sel(s));
endmodule

module mux4to1 (
  input  u,
  input  v,
  input  s0,
  input  w,
  input  x,
  input  s1,
  output m
);

  wire mux2to1_1_m, mux2to1_2_m;

  mux2to1 mux2to1_1 (.x(u), .y(v), .s(s0), .m(mux2to1_1_m));
  mux2to1 mux2to1_2 (.x(w), .y(x), .s(s0), .m(mux2to1_2_m));
  mux2to1 mux2to1_3 (.x(mux2to1_1_m), .y(mux2to1_2_m), .s(s1), .m(m));
endmodule
