// Logisim project Lab5Part1.circ as structural Verilog: 10 circuits, main circuit eight_bits_counter
module eight_bits_counter (
  input  Enable,
  input  Clock,
  input  Clear_b,
  output Q7,
  output Q6,
  output Q5,
  output Q4,
  output Q3,
  output Q2,
  output Q1,
  output Q0
);

  wire and_1_out, and_2_out, and_3_out, and_4_out, and_5_out, and_6_out, and_7_out, not_1_out, t_ff_8_q;

  T_Flip_Flop t_ff_1 (.T(Enable), .clk(Clock), .Q(Q7), .reset(not_1_out));  // open: Qn, preset
  not not_1 (not_1_out, Clear_b);
  and and_1 (and_1_out, Enable, Q7);
  T_Flip_Flop t_ff_2 (.T(and_1_out), .clk(Clock), .Q(Q6), .reset(not_1_out));  // open: Qn, preset
  and and_2 (and_2_out, and_1_out, Q6);
  T_Flip_Flop t_ff_3 (.T(and_2_out), .clk(Clock), .Q(Q5), .reset(not_1_out));  // open: Qn, preset
  and and_3 (and_3_out, and_2_out, Q5);
  T_Flip_Flop t_ff_4 (.T(and_3_out), .clk(Clock), .Q(Q4), .reset(not_1_out));  // open: Qn, preset
  and and_4 (and_4_out, and_3_out, Q4);
  T_Flip_Flop t_ff_5 (.T(and_4_out), .clk(Clock), .Q(Q3), .reset(not_1_out));  // open: Qn, preset
  and and_5 (and_5_out, and_4_out, Q3);
  T_Flip_Flop t_ff_6 (.T(and_5_out), .clk(Clock), .Q(Q2), .reset(not_1_out));  // open: Qn, preset
  and and_6 (and_6_out, and_5_out, Q2);
  T_Flip_Flop t_ff_7 (.T(and_6_out), .clk(Clock), .Q(Q1), .reset(not_1_out));  // open: Qn, preset
  and and_7 (and_7_out, and_6_out, Q1);
  T_Flip_Flop t_ff_8 (.T(and_7_out), .clk(Clock), .Q(t_ff_8_q), .reset(not_1_out));  // open: Qn, preset
  and and_8 (Q0, and_7_out, t_ff_8_q);
endmodule

module HaxDecoder (
  input  SW3,
  input  SW2,
  input  SW1,
  input  SW0,
  output HEX0,
  output HEX1,
  output HEX2,
  output HEX3,
  output HEX4,
  output HEX5,
  output HEX6
);

  Segment0 segment0_1 (.SW3(SW3), .SW2(SW2), .SW1(SW1), .SW0(SW0), .HEX0(HEX0));
  Segment1 segment1_1 (.SW3(SW3), .SW2(SW2), .SW1(SW1), .SW0(SW0), .HEX1(HEX1));
  Segment2 segment2_1 (.SW3(SW3), .SW2(SW2), .SW1(SW1), .SW0(SW0), .HEX2(HEX2));
  Segment3 segment3_1 (.SW3(SW3), .SW2(SW2), .SW1(SW1), .SW0(SW0), .HEX3(HEX3));
  Segment4 segment4_1 (.SW3(SW3), .SW2(SW2), .SW1(SW1), .SW0(SW0), .HEX4(HEX4));
  Segment5 segment5_1 (.SW3(SW3), .SW2(SW2), .SW1(SW1), .SW0(SW0), .HEX5(HEX5));
  Segment6 segment6_1 (.SW3(SW3), .SW2(SW2), .SW1(SW1), .SW0(SW0), .HEX6(HEX6));
endmodule

module Segment0 (
  input  SW3,
  input  SW2,
  input  SW1,
  input  SW0,
  output HEX0
);

  wire and_1_out, and_2_out, and_3_out, and_4_out, and_5_out, and_6_out, not_1_out, not_2_out, not_3_out,
       not_4_out;

  not not_1 (not_1_out, SW3);
  not not_2 (not_2_out, SW2);
  not not_3 (not_3_out, SW1);
  not not_4 (not_4_out, SW0);
  and and_1 (and_1_out, SW1, not_1_out);
  and and_2 (and_2_out, not_4_out, SW3);
  and and_3 (and_3_out, not_4_out, not_2_out);
  and and_4 (and_4_out, SW0, SW2, not_1_out);
  and and_5 (and_5_out, SW1, SW2);
  and and_6 (and_6_out, not_3_out, not_2_out, SW3);
  or or_1 (HEX0, and_6_out, and_4_out, and_5_out, and_1_out, and_2_out, and_3_out);
endmodule

module Segment1 (
  input  SW3,
  input  SW2,
  input  SW1,
  input  SW0,
  output HEX1
);

  wire and_1_out, and_2_out, and_3_out, and_4_out, not_1_out, not_2_out, not_3_out, not_4_out, xnor_1_out;

  not not_1 (not_1_out, SW3);
  not not_2 (not_2_out, SW2);
  not not_3 (not_3_out, SW1);
  not not_4 (not_4_out, SW0);
  and and_1 (and_1_out, not_2_out, not_1_out);
  xnor xnor_1 (xnor_1_out, SW0, SW1);
  and and_2 (and_2_out, not_4_out, not_2_out);
  and and_3 (and_3_out, SW0, not_3_out, SW3);
  and and_4 (and_4_out, xnor_1_out, not_1_out);
  or or_1 (HEX1, and_2_out, and_3_out, and_4_out, and_1_out);
endmodule

module Segment2 (
  input  SW3,
  input  SW2,
  input  SW1,
  input  SW0,
  output HEX2
);

  wire and_1_out, and_2_out, not_1_out, not_2_out, not_3_out, not_4_out, or_1_out, xor_1_out;

  not not_1 (not_1_out, SW3);
  not not_2 (not_2_out, SW2);
  not not_3 (not_3_out, SW1);
  not not_4 (not_4_out, SW0);
  or or_1 (or_1_out, not_3_out, not_1_out);
  and and_1 (and_1_out, not_3_out, not_1_out);
  xor xor_1 (xor_1_out, SW2, SW3);
  and and_2 (and_2_out, or_1_out, SW0);
  or or_2 (HEX2, and_2_out, and_1_out, xor_1_out);
endmodule

module Segment3 (
  input  SW3,
  input  SW2,
  input  SW1,
  input  SW0,
  output HEX3
);

  wire and_1_out, and_2_out, and_3_out, and_4_out, not_1_out, not_2_out, not_3_out, not_4_out, or_1_out,
       xor_1_out;

  not not_1 (not_1_out, SW3);
  not not_2 (not_2_out, SW2);
  not not_3 (not_3_out, SW1);
  not not_4 (not_4_out, SW0);
  or or_1 (or_1_out, not_4_out, SW1);
  and and_1 (and_1_out, not_3_out, SW3);
  xor xor_1 (xor_1_out, SW0, SW1);
  and and_2 (and_2_out, or_1_out, not_2_out, not_1_out);
  and and_3 (and_3_out, SW0, not_2_out, SW3);
  and and_4 (and_4_out, xor_1_out, SW2);
  or or_2 (HEX3, and_3_out, and_1_out, and_4_out, and_2_out);
endmodule

module Segment4 (
  input  SW3,
  input  SW2,
  input  SW1,
  input  SW0,
  output HEX4
);

  wire and_1_out, and_2_out, not_1_out, not_2_out, not_3_out, not_4_out, or_1_out, or_2_out;

  not not_1 (not_1_out, SW3);
  not not_2 (not_2_out, SW2);
  not not_3 (not_3_out, SW1);
  not not_4 (not_4_out, SW0);
  or or_1 (or_1_out, SW1, SW2);
  or or_2 (or_2_out, SW1, not_2_out);
  and and_1 (and_1_out, or_2_out, not_4_out);
  and and_2 (and_2_out, or_1_out, SW3);
  or or_3 (HEX4, and_2_out, and_1_out);
endmodule

module Segment5 (
  input  SW3,
  input  SW2,
  input  SW1,
  input  SW0,
  output HEX5
);

  wire and_1_out, and_2_out, and_3_out, not_1_out, not_2_out, not_3_out, not_4_out, or_1_out, or_2_out;

  not not_1 (not_1_out, SW3);
  not not_2 (not_2_out, SW2);
  not not_3 (not_3_out, SW1);
  not not_4 (not_4_out, SW0);
  or or_1 (or_1_out, not_3_out, SW2);
  and and_1 (and_1_out, not_3_out, SW2, not_1_out);
  or or_2 (or_2_out, SW1, not_2_out);
  and and_2 (and_2_out, or_2_out, SW3);
  and and_3 (and_3_out, or_1_out, not_4_out);
  or or_3 (HEX5, and_1_out, and_2_out, and_3_out);
endmodule

module Segment6 (
  input  SW3,
  input  SW2,
  input  SW1,
  input  SW0,
  output HEX6
);

  wire and_1_out, and_2_out, and_3_out, not_1_out, not_2_out, not_3_out, not_4_out, or_1_out, or_2_out;

  not not_1 (not_1_out, SW3);
  not not_2 (not_2_out, SW2);
  not not_3 (not_3_out, SW1);
  not not_4 (not_4_out, SW0);
  or or_1 (or_1_out, not_4_out, not_2_out);
  and and_1 (and_1_out, not_3_out, SW2, not_1_out);
  or or_2 (or_2_out, SW0, SW1, not_2_out);
  and and_2 (and_2_out, or_1_out, SW1);
  and and_3 (and_3_out, or_2_out, SW3);
  or or_3 (HEX6, and_3_out, and_2_out, and_1_out);
endmodule

module main (
  input  Enable,
  input  Clock,
  input  Clear_b
);

  wire eight_bits_counter_1_q0, eight_bits_counter_1_q1, eight_bits_counter_1_q2, eight_bits_counter_1_q3,
       eight_bits_counter_1_q4, eight_bits_counter_1_q5, eight_bits_counter_1_q6, eight_bits_counter_1_q7,
       haxdecoder_1_hex0, haxdecoder_1_hex1, haxdecoder_1_hex2, haxdecoder_1_hex3, haxdecoder_1_hex4,
       haxdecoder_1_hex5, haxdecoder_1_hex6, haxdecoder_2_hex0, haxdecoder_2_hex1, haxdecoder_2_hex2,
       haxdecoder_2_hex3, haxdecoder_2_hex4, haxdecoder_2_hex5, haxdecoder_2_hex6;

  eight_bits_counter eight_bits_counter_1 (
    .Enable(Enable), .Clock(Clock), .Clear_b(Clear_b), .Q7(eight_bits_counter_1_q7),
    .Q6(eight_bits_counter_1_q6), .Q5(eight_bits_counter_1_q5), .Q4(eight_bits_counter_1_q4),
    .Q3(eight_bits_counter_1_q3), .Q2(eight_bits_counter_1_q2), .Q1(eight_bits_counter_1_q1),
    .Q0(eight_bits_counter_1_q0));
  HaxDecoder haxdecoder_1 (
    .SW3(eight_bits_counter_1_q4), .SW2(eight_bits_counter_1_q5), .SW1(eight_bits_counter_1_q6),
    .SW0(eight_bits_counter_1_q7), .HEX0(haxdecoder_1_hex0), .HEX1(haxdecoder_1_hex1),
    .HEX2(haxdecoder_1_hex2), .HEX3(haxdecoder_1_hex3), .HEX4(haxdecoder_1_hex4), .HEX5(haxdecoder_1_hex5),
    .HEX6(haxdecoder_1_hex6));
  HaxDecoder haxdecoder_2 (
    .SW3(eight_bits_counter_1_q0), .SW2(eight_bits_counter_1_q1), .SW1(eight_bits_counter_1_q2),
    .SW0(eight_bits_counter_1_q3), .HEX0(haxdecoder_2_hex0), .HEX1(haxdecoder_2_hex1),
    .HEX2(haxdecoder_2_hex2), .HEX3(haxdecoder_2_hex3), .HEX4(haxdecoder_2_hex4), .HEX5(haxdecoder_2_hex5),
    .HEX6(haxdecoder_2_hex6));
  _7_Segment_Display u_7_segment_display_1 (
    .g(haxdecoder_1_hex6), .f(haxdecoder_1_hex5), .a(haxdecoder_1_hex0), .b(haxdecoder_1_hex1),
    .e(haxdecoder_1_hex4), .d(haxdecoder_1_hex3), .c(haxdecoder_1_hex2));  // open: dp
  _7_Segment_Display u_7_segment_display_2 (
    .g(haxdecoder_2_hex6), .f(haxdecoder_2_hex5), .a(haxdecoder_2_hex0), .b(haxdecoder_2_hex1),
    .e(haxdecoder_2_hex4), .d(haxdecoder_2_hex3), .c(haxdecoder_2_hex2));  // open: dp
endmodule
