// Logisim project Lab5Part2.circ as structural Verilog: 15 circuits, main circuit main
module main (
  input  Reset,
  input  [1:0] SW
);

  wire clock_1_out, haxdecoder_1_hex0, haxdecoder_1_hex1, haxdecoder_1_hex2, haxdecoder_1_hex3,
       haxdecoder_1_hex4, haxdecoder_1_hex5, haxdecoder_1_hex6, not_1_out, ratedivider_1_clk_out;
  wire [3:0] displaycounter_1_hex;

  Clock clock_1 (.out(clock_1_out));
  not not_1 (not_1_out, clock_1_out);
  RateDivider ratedivider_1 (.Clk_in(clock_1_out), .Reset(Reset), .SW(SW), .Clk_out(ratedivider_1_clk_out));
  DisplayCounter displaycounter_1 (
    .Reset(Reset), .Enable(ratedivider_1_clk_out), .Clk(not_1_out), .HEX(displaycounter_1_hex));
  HaxDecoder haxdecoder_1 (
    .SW3(displaycounter_1_hex[3]), .SW2(displaycounter_1_hex[2]), .SW1(displaycounter_1_hex[1]),
    .SW0(displaycounter_1_hex[0]), .HEX0(haxdecoder_1_hex0), .HEX1(haxdecoder_1_hex1),
    .HEX2(haxdecoder_1_hex2), .HEX3(haxdecoder_1_hex3), .HEX4(haxdecoder_1_hex4), .HEX5(haxdecoder_1_hex5),
    .HEX6(haxdecoder_1_hex6));
  _7_Segment_Display u_7_segment_display_1 (
    .g(haxdecoder_1_hex6), .f(haxdecoder_1_hex5), .a(haxdecoder_1_hex0), .b(haxdecoder_1_hex1),
    .e(haxdecoder_1_hex4), .d(haxdecoder_1_hex3), .c(haxdecoder_1_hex2));  // open: dp
endmodule

module RateDivider (
  input  Clk_in,
  input  Reset,
  input  [1:0] SW,
  output Clk_out
);

  wire clock16_to_1_1_clk_out, clock16_to_d5_1_clk_out, clock16_to_d25_1_clk_out;

  Clock16_to_1 clock16_to_1_1 (.Reset(Reset), .Clk_in(Clk_in), .Clk_out(clock16_to_1_1_clk_out));
  Clock16_to_d5 clock16_to_d5_1 (.Reset(Reset), .Clk_in(Clk_in), .Clk_out(clock16_to_d5_1_clk_out));
  Clock16_to_d25 clock16_to_d25_1 (.Reset(Reset), .Clk_in(Clk_in), .Clk_out(clock16_to_d25_1_clk_out));
  Multiplexer #(.enable("false"), .select(2)) multiplexer_1 (
    .in0(Clk_in), .in1(clock16_to_1_1_clk_out), .in2(clock16_to_d5_1_clk_out),
    .in3(clock16_to_d25_1_clk_out), .out(Clk_out), .sel(SW));
endmodule

module example_counter (
  input  R,
  input  Enable,
  input  Clk,
  output counter_out
);

  wire not_1_out, or_1_out;
  wire [3:0] counter_1_q;

  not not_1 (not_1_out, Enable);
  or or_1 (or_1_out, counter_out, not_1_out);
  Counter #(.max('hf), .width(4)) counter_1 (
    .clr(R), .load(or_1_out), .up(1'b1), .clk(Clk), .D(4'b0110), .Q(counter_1_q));  // open: count, carry
  and and_1 (counter_out, counter_1_q[0], counter_1_q[1], counter_1_q[2], counter_1_q[3]);
endmodule

module Clock16_to_1 (
  input  Reset,
  input  Clk_in,
  output Clk_out
);

  wire [3:0] counter_1_q;

  Counter #(.max('hf), .width(4)) counter_1 (
    .clr(Reset), .load(Clk_out), .up(1'b1), .clk(Clk_in), .D(4'b0000), .Q(counter_1_q));  // open: count, carry
  and and_1 (Clk_out, counter_1_q[0], counter_1_q[1], counter_1_q[2], counter_1_q[3]);
endmodule

module Clock16_to_d5 (
  input  Reset,
  input  Clk_in,
  output Clk_out
);

  wire [4:0] counter_1_q;

  Counter #(.max('h1f), .width(5)) counter_1 (
    .clr(Reset), .load(Clk_out), .up(1'b1), .clk(Clk_in), .D({5{1'b0}}), .Q(counter_1_q));  // open: count, carry
  and and_1 (Clk_out, counter_1_q[0], counter_1_q[1], counter_1_q[2], counter_1_q[3], counter_1_q[4]);
endmodule

module Clock16_to_d25 (
  input  Reset,
  input  Clk_in,
  output Clk_out
);

  wire [5:0] counter_1_q;

  Counter #(.max('h3f), .width(6)) counter_1 (
    .clr(Reset), .load(Clk_out), .up(1'b1), .clk(Clk_in), .D({6{1'b0}}), .Q(counter_1_q));  // open: count, carry
  and and_1 (Clk_out, counter_1_q[0], counter_1_q[1], counter_1_q[2], counter_1_q[3], counter_1_q[4], counter_1_q[5]);
endmodule

module DisplayCounter (
  input  Reset,
  input  Enable,
  input  Clk,
  output [3:0] HEX
);

  wire not_1_out;

  not not_1 (not_1_out, Enable);
  Counter #(.max('hf), .width(4)) counter_1 (
    .clr(Reset), .load(not_1_out), .up(1'b1), .clk(Clk), .D(HEX), .Q(HEX));  // open: count, carry
endmodule

module HaxDecoder (
  input  SW3,
  input  SW2,
  input  SW1,
  input  SW0,
  output HEX0,
  output HEX1,
  output HEX2,
  output HEX3,
  output HEX4,
  output HEX5,
  output HEX6
);

  Segment0 segment0_1 (.SW3(SW3), .SW2(SW2), .SW1(SW1), .SW0(SW0), .HEX0(HEX0));
  Segment1 segment1_1 (.SW3(SW3), .SW2(SW2), .SW1(SW1), .SW0(SW0), .HEX1(HEX1));
  Segment2 segment2_1 (.SW3(SW3), .SW2(SW2), .SW1(SW1), .SW0(SW0), .HEX2(HEX2));
  Segment3 segment3_1 (.SW3(SW3), .SW2(SW2), .SW1(SW1), .SW0(SW0), .HEX3(HEX3));
  Segment4 segment4_1 (.SW3(SW3), .SW2(SW2), .SW1(SW1), .SW0(SW0), .HEX4(HEX4));
  Segment5 segment5_1 (.SW3(SW3), .SW2(SW2), .SW1(SW1), .SW0(SW0), .HEX5(HEX5));
  Segment6 segment6_1 (.SW3(SW3), .SW2(SW2), .SW1(SW1), .SW0(SW0), .HEX6(HEX6));
endmodule

module Segment0 (
  input  SW3,
  input  SW2,
  input  SW1,
  input  SW0,
  output HEX0
);

  wire and_1_out, and_2_out, and_3_out, and_4_out, and_5_out, and_6_out, not_1_out, not_2_out, not_3_out,
       not_4_out;

  not not_1 (not_1_out, SW3);
  not not_2 (not_2_out, SW2);
  not not_3 (not_3_out, SW1);
  not not_4 (not_4_out, SW0);
  and and_1 (and_1_out, SW1, not_1_out);
  and and_2 (and_2_out, not_4_out, SW3);
  and and_3 (and_3_out, not_4_out, not_2_out);
  and and_4 (and_4_out, SW0, SW2, not_1_out);
  and and_5 (and_5_out, SW1, SW2);
  and and_6 (and_6_out, not_3_out, not_2_out, SW3);
  or or_1 (HEX0, and_6_out, and_4_out, and_5_out, and_1_out, and_2_out, and_3_out);
endmodule

module Segment1 (
  input  SW3,
  input  SW2,
  input  SW1,
  input  SW0,
  output HEX1
);

  wire and_1_out, and_2_out, and_3_out, and_4_out, not_1_out, not_2_out, not_3_out, not_4_out, xnor_1_out;

  not not_1 (not_1_out, SW3);
  not not_2 (not_2_out, SW2);
  not not_3 (not_3_out, SW1);
  not not_4 (not_4_out, SW0);
  and and_1 (and_1_out, not_2_out, not_1_out);
  xnor xnor_1 (xnor_1_out, SW0, SW1);
  and and_2 (and_2_out, not_4_out, not_2_out);
  and and_3 (and_3_out, SW0, not_3_out, SW3);
  and and_4 (and_4_out, xnor_1_out, not_1_out);
  or or_1 (HEX1, and_2_out, and_3_out, and_4_out, and_1_out);
endmodule

module Segment2 (
  input  SW3,
  input  SW2,
  input  SW1,
  input  SW0,
  output HEX2
);

  wire and_1_out, and_2_out, not_1_out, not_2_out, not_3_out, not_4_out, or_1_out, xor_1_out;

  not not_1 (not_1_out, SW3);
  not not_2 (not_2_out, SW2);
  not not_3 (not_3_out, SW1);
  not not_4 (not_4_out, SW0);
  or or_1 (or_1_out, not_3_out, not_1_out);
  and and_1 (and_1_out, not_3_out, not_1_out);
  xor xor_1 (xor_1_out, SW2, SW3);
  and and_2 (and_2_out, or_1_out, SW0);
  or or_2 (HEX2, and_2_out, and_1_out, xor_1_out);
endmodule

module Segment3 (
  input  SW3,
  input  SW2,
  input  SW1,
  input  SW0,
  output HEX3
);

  wire and_1_out, and_2_out, and_3_out, and_4_out, not_1_out, not_2_out, not_3_out, not_4_out, or_1_out,
       xor_1_out;

  not not_1 (not_1_out, SW3);
  not not_2 (not_2_out, SW2);
  not not_3 (not_3_out, SW1);
  not not_4 (not_4_out, SW0);
  or or_1 (or_1_out, not_4_out, SW1);
  and and_1 (and_1_out, not_3_out, SW3);
  xor xor_1 (xor_1_out, SW0, SW1);
  and and_2 (and_2_out, or_1_out, not_2_out, not_1_out);
  and and_3 (and_3_out, SW0, not_2_out, SW3);
  and and_4 (and_4_out, xor_1_out, SW2);
  or or_2 (HEX3, and_3_out, and_1_out, and_4_out, and_2_out);
endmodule

module Segment4 (
  input  SW3,
  input  SW2,
  input  SW1,
  input  SW0,
  output HEX4
);

  wire and_1_out, and_2_out, not_1_out, not_2_out, not_3_out, not_4_out, or_1_out, or_2_out;

  not not_1 (not_1_out, SW3);
  not not_2 (not_2_out, SW2);
  not not_3 (not_3_out, SW1);
  not not_4 (not_4_out, SW0);
  or or_1 (or_1_out, SW1, SW2);
  or or_2 (or_2_out, SW1, not_2_out);
  and and_1 (and_1_out, or_2_out, not_4_out);
  and and_2 (and_2_out, or_1_out, SW3);
  or or_3 (HEX4, and_2_out, and_1_out);
endmodule

module Segment5 (
  input  SW3,
  input  SW2,
  input  SW1,
  input  SW0,
  output HEX5
);

  wire and_1_out, and_2_out, and_3_out, not_1_out, not_2_out, not_3_out, not_4_out, or_1_out, or_2_out;

  not not_1 (not_1_out, SW3);
  not not_2 (not_2_out, SW2);
  not not_3 (not_3_out, SW1);
  not not_4 (not_4_out, SW0);
  or or_1 (or_1_out, not_3_out, SW2);
  and and_1 (and_1_out, not_3_out, SW2, not_1_out);
  or or_2 (or_2_out, SW1, not_2_out);
  and and_2 (and_2_out, or_2_out, SW3);
  and and_3 (and_3_out, or_1_out, not_4_out);
  or or_3 (HEX5, and_1_out, and_2_out, and_3_out);
endmodule

module Segment6 (
  input  SW3,
  input  SW2,
  input  SW1,
  input  SW0,
  output HEX6
);

  wire and_1_out, and_2_out, and_3_out, not_1_out, not_2_out, not_3_out, not_4_out, or_1_out, or_2_out;

  not not_1 (not_1_out, SW3);
  not not_2 (not_2_out, SW2);
  not not_3 (not_3_out, SW1);
  not not_4 (not_4_out, SW0);
  or or_1 (or_1_out, not_4_out, not_2_out);
  and and_1 (and_1_out, not_3_out, SW2, not_1_out);
  or or_2 (or_2_out, SW0, SW1, not_2_out);
  and and_2 (and_2_out, or_1_out, SW1);
  and and_3 (and_3_out, or_2_out, SW3);
  or or_3 (HEX6, and_3_out, and_2_out, and_1_out);
endmodule
