// Logisim project Lab5Part3.circ as structural Verilog: 5 circuits, main circuit main
module main (
  input  [2:0] SW,
  input  KEY1,
  input  KEY0
);

  wire clock_1_out, morse_code_encoder_1_ledr;

  Clock clock_1 (.out(clock_1_out));
  LED led_1 (.in(morse_code_encoder_1_ledr));
  morse_code_encoder morse_code_encoder_1 (
    .SW(SW), .KEY1(KEY1), .KEY0(KEY0), .Clk(clock_1_out), .LEDR(morse_code_encoder_1_ledr));
endmodule

module LUT (
  input  [2:0] SW,
  output [12:0] LUT_out
);

  Multiplexer #(.enable("false"), .select(3), .width(13)) multiplexer_1 (
    .in0(13'h1500), .in1(13'h1c00), .in2(13'h15c0), .in3(13'h1570), .in4(13'h1770), .in5(13'h1d5c),
    .in6(13'h1d77), .in7(13'h1dd4), .out(LUT_out), .sel(SW));
endmodule

module shift_register (
  input  Reset,
  input  Enable,
  input  Clk,
  input  [12:0] LUT_in,
  output LEDR
);

  wire shift_register_1_p2;

  // Shift_Register #(.length(13)) shift_register_1: pin names not known; wires that end beside it: Reset, shift_register_1_p2, Enable, Clk, 1'b0, LUT_in[0], LUT_in[1], LUT_in[2], LUT_in[3], LUT_in[4], LUT_in[5], LUT_in[6], LUT_in[7], LUT_in[8], LUT_in[9], LUT_in[10], LUT_in[11]
  not not_1 (shift_register_1_p2, Enable);
endmodule

module rate_divider (
  input  Reset,
  input  Clk_in,
  output Clk_out
);

  wire [2:0] counter_1_q;

  Counter #(.max('h7), .width(3)) counter_1 (
    .clr(Reset), .load(Clk_out), .up(1'b1), .clk(Clk_in), .D(3'b000), .Q(counter_1_q));  // open: count, carry
  and and_1 (Clk_out, counter_1_q[0], counter_1_q[1], counter_1_q[2]);
endmodule

module morse_code_encoder (
  input  [2:0] SW,
  input  KEY1,
  input  KEY0,
  input  Clk,
  output LEDR
);

  wire rate_divider_1_clk_out;
  wire [12:0] lut_1_lut_out;

  LUT lut_1 (.SW(SW), .LUT_out(lut_1_lut_out));
  rate_divider rate_divider_1 (.Reset(KEY0), .Clk_in(Clk), .Clk_out(rate_divider_1_clk_out));
  shift_register shift_register_1 (
    .Reset(KEY0), .Enable(KEY1), .Clk(rate_divider_1_clk_out), .LUT_in(lut_1_lut_out), .LEDR(LEDR));
endmodule
