// Logisim project Lab7.circ as structural Verilog: 12 circuits, main circuit main
module main (
  input  Reset,
  input  Enable
);

  wire clock_1_out, haxdecoder_1_hex0, haxdecoder_1_hex1, haxdecoder_1_hex2, haxdecoder_1_hex3,
       haxdecoder_1_hex4, haxdecoder_1_hex5, haxdecoder_1_hex6;
  wire [3:0] increasingvalue_1_p1;

  Clock clock_1 (.out(clock_1_out));
  // IncreasingValue increasingvalue_1: pin names not known; wires that end beside it: increasingvalue_1_p1
  HaxDecoder haxdecoder_1 (
    .SW3(increasingvalue_1_p1[3]), .SW2(increasingvalue_1_p1[2]), .SW1(increasingvalue_1_p1[1]),
    .SW0(increasingvalue_1_p1[0]), .HEX0(haxdecoder_1_hex0), .HEX1(haxdecoder_1_hex1),
    .HEX2(haxdecoder_1_hex2), .HEX3(haxdecoder_1_hex3), .HEX4(haxdecoder_1_hex4), .HEX5(haxdecoder_1_hex5),
    .HEX6(haxdecoder_1_hex6));
  _7_Segment_Display u_7_segment_display_1 (
    .g(haxdecoder_1_hex6), .f(haxdecoder_1_hex5), .a(haxdecoder_1_hex0), .b(haxdecoder_1_hex1),
    .e(haxdecoder_1_hex4), .d(haxdecoder_1_hex3), .c(haxdecoder_1_hex2));  // open: dp
endmodule

module RAM_32x4 (
  input  [4:0] Address,
  input  [3:0] DataIn,
  input  WriteEn,
  input  Clock,
  output [3:0] DataOut
);

  wire not_1_out, not_2_out, register_3_q;
  wire [3:0] register_2_q;
  wire [4:0] register_1_q;

  not not_1 (not_1_out, Clock);
  Register #(.width(5)) register_1 (.D(Address), .clk(not_1_out), .Q(register_1_q));  // open: en, clr
  Register #(.width(4)) register_2 (.D(DataIn), .clk(not_1_out), .Q(register_2_q));  // open: en, clr
  Register #(.width(1)) register_3 (.D(WriteEn), .clk(not_1_out), .Q(register_3_q));  // open: en, clr
  not not_2 (not_2_out, register_3_q);
  RAM #(.addrWidth(5), .dataWidth(4)) ram_1 (
    .addr(register_1_q), .we(register_3_q), .oe(not_2_out), .clk(Clock), .din(register_2_q), .dout(DataOut));
endmodule

module Test_ram (
  input  [4:0] Address,
  input  [3:0] DataIn,
  input  WriteEn,
  input  Clock,
  output [3:0] DataOut
);

  wire not_1_out, register_3_q;
  wire [3:0] register_2_q;
  wire [4:0] register_1_q;

  not not_1 (not_1_out, Clock);
  Register #(.width(5)) register_1 (.D(Address), .clk(not_1_out), .Q(register_1_q));  // open: en, clr
  Register #(.width(4)) register_2 (.D(DataIn), .clk(not_1_out), .Q(register_2_q));  // open: en, clr
  Register #(.width(1)) register_3 (.D(WriteEn), .clk(not_1_out), .Q(register_3_q));  // open: en, clr
  RAM #(.addrWidth(5), .dataWidth(4)) ram_1 (
    .addr(register_1_q), .we(register_3_q), .oe(register_3_q), .clk(Clock), .din(register_2_q), .dout(DataOut));
endmodule

module IncreasingValue (
  input  Reset,
  input  Enable,
  input  WriteEn
);

  wire clock_1_out, haxdecoder_1_hex0, haxdecoder_1_hex1, haxdecoder_1_hex2, haxdecoder_1_hex3,
       haxdecoder_1_hex4, haxdecoder_1_hex5, haxdecoder_1_hex6, not_1_out, not_2_out, register_3_q;
  wire [3:0] counter_1_q, ram_1_dout, register_2_q;
  wire [4:0] counter_2_q, register_1_q;

  Clock clock_1 (.out(clock_1_out));
  not not_1 (not_1_out, Enable);
  Counter #(.max('hf), .width(4)) counter_1 (
    .clr(Reset), .load(not_1_out), .clk(clock_1_out), .D(4'b0000), .Q(counter_1_q));  // open: up, count, carry
  Counter #(.max('h1f), .width(5)) counter_2 (
    .clr(Reset), .load(not_1_out), .clk(clock_1_out), .D({5{1'b0}}), .Q(counter_2_q));  // open: up, count, carry
  Register #(.width(5)) register_1 (.D(counter_2_q), .clk(clock_1_out), .Q(register_1_q));  // open: en, clr
  Register #(.width(4)) register_2 (.D(counter_1_q), .clk(clock_1_out), .Q(register_2_q));  // open: en, clr
  Register #(.width(1)) register_3 (.D(WriteEn), .clk(clock_1_out), .Q(register_3_q));  // open: en, clr
  RAM #(.addrWidth(5), .dataWidth(4)) ram_1 (
    .addr(register_1_q), .we(register_3_q), .oe(not_2_out), .clk(clock_1_out), .din(register_2_q),
    .dout(ram_1_dout));
  not not_2 (not_2_out, register_3_q);
  HaxDecoder haxdecoder_1 (
    .SW3(ram_1_dout[3]), .SW2(ram_1_dout[2]), .SW1(ram_1_dout[1]), .SW0(ram_1_dout[0]),
    .HEX0(haxdecoder_1_hex0), .HEX1(haxdecoder_1_hex1), .HEX2(haxdecoder_1_hex2), .HEX3(haxdecoder_1_hex3),
    .HEX4(haxdecoder_1_hex4), .HEX5(haxdecoder_1_hex5), .HEX6(haxdecoder_1_hex6));
  _7_Segment_Display u_7_segment_display_1 (
    .g(haxdecoder_1_hex6), .f(haxdecoder_1_hex5), .a(haxdecoder_1_hex0), .b(haxdecoder_1_hex1),
    .e(haxdecoder_1_hex4), .d(haxdecoder_1_hex3), .c(haxdecoder_1_hex2));  // open: dp
endmodule

module HaxDecoder (
  input  SW3,
  input  SW2,
  input  SW1,
  input  SW0,
  output HEX0,
  output HEX1,
  output HEX2,
  output HEX3,
  output HEX4,
  output HEX5,
  output HEX6
);

  Segment0 segment0_1 (.SW3(SW3), .SW2(SW2), .SW1(SW1), .SW0(SW0), .HEX0(HEX0));
  Segment1 segment1_1 (.SW3(SW3), .SW2(SW2), .SW1(SW1), .SW0(SW0), .HEX1(HEX1));
  Segment2 segment2_1 (.SW3(SW3), .SW2(SW2), .SW1(SW1), .SW0(SW0), .HEX2(HEX2));
  Segment3 segment3_1 (.SW3(SW3), .SW2(SW2), .SW1(SW1), .SW0(SW0), .HEX3(HEX3));
  Segment4 segment4_1 (.SW3(SW3), .SW2(SW2), .SW1(SW1), .SW0(SW0), .HEX4(HEX4));
  Segment5 segment5_1 (.SW3(SW3), .SW2(SW2), .SW1(SW1), .SW0(SW0), .HEX5(HEX5));
  Segment6 segment6_1 (.SW3(SW3), .SW2(SW2), .SW1(SW1), .SW0(SW0), .HEX6(HEX6));
endmodule

module Segment0 (
  input  SW3,
  input  SW2,
  input  SW1,
  input  SW0,
  output HEX0
);

  wire and_1_out, and_2_out, and_3_out, and_4_out, and_5_out, and_6_out, not_1_out, not_2_out, not_3_out,
       not_4_out;

  not not_1 (not_1_out, SW3);
  not not_2 (not_2_out, SW2);
  not not_3 (not_3_out, SW1);
  not not_4 (not_4_out, SW0);
  and and_1 (and_1_out, SW1, not_1_out);
  and and_2 (and_2_out, not_4_out, SW3);
  and and_3 (and_3_out, not_4_out, not_2_out);
  and and_4 (and_4_out, SW0, SW2, not_1_out);
  and and_5 (and_5_out, SW1, SW2);
  and and_6 (and_6_out, not_3_out, not_2_out, SW3);
  or or_1 (HEX0, and_6_out, and_4_out, and_5_out, and_1_out, and_2_out, and_3_out);
endmodule

module Segment1 (
  input  SW3,
  input  SW2,
  input  SW1,
  input  SW0,
  output HEX1
);

  wire and_1_out, and_2_out, and_3_out, and_4_out, not_1_out, not_2_out, not_3_out, not_4_out, xnor_1_out;

  not not_1 (not_1_out, SW3);
  not not_2 (not_2_out, SW2);
  not not_3 (not_3_out, SW1);
  not not_4 (not_4_out, SW0);
  and and_1 (and_1_out, not_2_out, not_1_out);
  xnor xnor_1 (xnor_1_out, SW0, SW1);
  and and_2 (and_2_out, not_4_out, not_2_out);
  and and_3 (and_3_out, SW0, not_3_out, SW3);
  and and_4 (and_4_out, xnor_1_out, not_1_out);
  or or_1 (HEX1, and_2_out, and_3_out, and_4_out, and_1_out);
endmodule

module Segment2 (
  input  SW3,
  input  SW2,
  input  SW1,
  input  SW0,
  output HEX2
);

  wire and_1_out, and_2_out, not_1_out, not_2_out, not_3_out, not_4_out, or_1_out, xor_1_out;

  not not_1 (not_1_out, SW3);
  not not_2 (not_2_out, SW2);
  not not_3 (not_3_out, SW1);
  not not_4 (not_4_out, SW0);
  or or_1 (or_1_out, not_3_out, not_1_out);
  and and_1 (and_1_out, not_3_out, not_1_out);
  xor xor_1 (xor_1_out, SW2, SW3);
  and and_2 (and_2_out, or_1_out, SW0);
  or or_2 (HEX2, and_2_out, and_1_out, xor_1_out);
endmodule

module Segment3 (
  input  SW3,
  input  SW2,
  input  SW1,
  input  SW0,
  output HEX3
);

  wire and_1_out, and_2_out, and_3_out, and_4_out, not_1_out, not_2_out, not_3_out, not_4_out, or_1_out,
       xor_1_out;

  not not_1 (not_1_out, SW3);
  not not_2 (not_2_out, SW2);
  not not_3 (not_3_out, SW1);
  not not_4 (not_4_out, SW0);
  or or_1 (or_1_out, not_4_out, SW1);
  and and_1 (and_1_out, not_3_out, SW3);
  xor xor_1 (xor_1_out, SW0, SW1);
  and and_2 (and_2_out, or_1_out, not_2_out, not_1_out);
  and and_3 (and_3_out, SW0, not_2_out, SW3);
  and and_4 (and_4_out, xor_1_out, SW2);
  or or_2 (HEX3, and_3_out, and_1_out, and_4_out, and_2_out);
endmodule

module Segment4 (
  input  SW3,
  input  SW2,
  input  SW1,
  input  SW0,
  output HEX4
);

  wire and_1_out, and_2_out, not_1_out, not_2_out, not_3_out, not_4_out, or_1_out, or_2_out;

  not not_1 (not_1_out, SW3);
  not not_2 (not_2_out, SW2);
  not not_3 (not_3_out, SW1);
  not not_4 (not_4_out, SW0);
  or or_1 (or_1_out, SW1, SW2);
  or or_2 (or_2_out, SW1, not_2_out);
  and and_1 (and_1_out, or_2_out, not_4_out);
  and and_2 (and_2_out, or_1_out, SW3);
  or or_3 (HEX4, and_2_out, and_1_out);
endmodule

module Segment5 (
  input  SW3,
  input  SW2,
  input  SW1,
  input  SW0,
  output HEX5
);

  wire and_1_out, and_2_out, and_3_out, not_1_out, not_2_out, not_3_out, not_4_out, or_1_out, or_2_out;

  not not_1 (not_1_out, SW3);
  not not_2 (not_2_out, SW2);
  not not_3 (not_3_out, SW1);
  not not_4 (not_4_out, SW0);
  or or_1 (or_1_out, not_3_out, SW2);
  and and_1 (and_1_out, not_3_out, SW2, not_1_out);
  or or_2 (or_2_out, SW1, not_2_out);
  and and_2 (and_2_out, or_2_out, SW3);
  and and_3 (and_3_out, or_1_out, not_4_out);
  or or_3 (HEX5, and_1_out, and_2_out, and_3_out);
endmodule

module Segment6 (
  input  SW3,
  input  SW2,
  input  SW1,
  input  SW0,
  output HEX6
);

  wire and_1_out, and_2_out, and_3_out, not_1_out, not_2_out, not_3_out, not_4_out, or_1_out, or_2_out;

  not not_1 (not_1_out, SW3);
  not not_2 (not_2_out, SW2);
  not not_3 (not_3_out, SW1);
  not not_4 (not_4_out, SW0);
  or or_1 (or_1_out, not_4_out, not_2_out);
  and and_1 (and_1_out, not_3_out, SW2, not_1_out);
  or or_2 (or_2_out, SW0, SW1, not_2_out);
  and and_2 (and_2_out, or_1_out, SW1);
  and and_3 (and_3_out, or_2_out, SW3);
  or or_3 (HEX6, and_3_out, and_2_out, and_1_out);
endmodule
