// Logisim project Lab7Part2.circ as structural Verilog: 5 circuits, main circuit main
module main (
  input  Reset,
  input  Enable,
  input  [6:0] Y,
  input  [6:0] X
);

  wire clock_1_out, clock_2_out, datapath_1_writeen, fsm_1_change_color, fsm_1_en;
  wire [6:0] datapath_1_x_out, datapath_1_y_out;
  wire [23:0] datapath_1_rgb;

  Clock clock_1 (.out(clock_1_out));
  Clock clock_2 (.out(clock_2_out));
  FSM fsm_1 (.Enable(Enable), .Clock(clock_1_out), .Reset(Reset), .En(fsm_1_en), .Change_color(fsm_1_change_color));
  Datapath datapath_1 (
    .Enable(fsm_1_en), .Y_in(Y), .Clock(clock_2_out), .X_in(X), .RGB_random(fsm_1_change_color),
    .WriteEn(datapath_1_writeen), .Y_out(datapath_1_y_out), .X_out(datapath_1_x_out), .RGB(datapath_1_rgb));
  // RGB_Video rgb_video_1: pin names not known; wires that end beside it: Reset, clock_1_out, datapath_1_writeen, datapath_1_x_out, datapath_1_y_out, datapath_1_rgb
endmodule

module Datapath (
  input  Enable,
  input  [6:0] Y_in,
  input  Clock,
  input  [6:0] X_in,
  input  RGB_random,
  output WriteEn,
  output [6:0] Y_out,
  output [6:0] X_out,
  output [23:0] RGB
);

  wire and_1_out, d_ff_1_q, not_1_out;
  wire [3:0] counter_1_q, counter_2_q;
  wire [6:0] bit_extender_1_out, bit_extender_2_out;

  not not_1 (not_1_out, Enable);
  Counter #(.max('hf), .width(4)) counter_1 (
    .clr(not_1_out), .clk(d_ff_1_q), .D(4'b0000), .Q(counter_1_q));  // open: load, up, count, carry
  D_Flip_Flop d_ff_1 (.D(and_1_out), .clk(Clock), .Q(d_ff_1_q));  // open: Qn, preset, reset
  Counter #(.max('hf), .width(4)) counter_2 (
    .clr(not_1_out), .clk(Clock), .D(4'b0000), .Q(counter_2_q));  // open: load, up, count, carry
  Random #(.width(24)) random_1 (.clk(RGB_random), .out(RGB));  // open: clr, next
  assign bit_extender_1_out = {{3{1'b0}}, counter_1_q};  // Bit_Extender bit_extender_1
  and and_1 (and_1_out, counter_2_q[3], counter_2_q[2], counter_2_q[1], counter_2_q[0]);
  assign bit_extender_2_out = {{3{1'b0}}, counter_2_q};  // Bit_Extender bit_extender_2
  Adder #(.width(7)) adder_1 (.a(Y_in), .b(bit_extender_1_out), .out(Y_out));  // open: cin, cout
  Adder #(.width(7)) adder_2 (.a(bit_extender_2_out), .b(X_in), .out(X_out));  // open: cin, cout

  assign WriteEn = Enable;
endmodule

module Test (
  input  Reset,
  input  WriteEn,
  input  [6:0] Y,
  input  [6:0] X,
  input  [23:0] RGB
);

  wire rgb_video_1_p2;

  // RGB_Video rgb_video_1: pin names not known; wires that end beside it: Reset, rgb_video_1_p2, WriteEn, X, Y, RGB
  Clock clock_1 (.out(rgb_video_1_p2));
endmodule

module FSM (
  input  Enable,
  input  Clock,
  input  Reset,
  output En,
  output Change_color
);

  wire multiplexer_1_out, register_1_q, state_table_1_next_state;

  State_table state_table_1 (
    .State(multiplexer_1_out), .Enable(En), .Change_color(Change_color), .Next_state(state_table_1_next_state));
  Register #(.width(1)) register_1 (
    .D(state_table_1_next_state), .en(Enable), .clk(Clock), .Q(register_1_q), .clr(Reset));
  Multiplexer #(.enable("false")) multiplexer_1 (.in0(1'b0), .in1(register_1_q), .out(multiplexer_1_out), .sel(Enable));
endmodule

module State_table (
  input  State,
  output Enable,
  output Change_color,
  output Next_state
);

  wire not_1_out;

  not not_1 (not_1_out, State);
  not not_2 (Change_color, State);
  or or_1 (Next_state, not_1_out, State);

  assign Enable = State;
endmodule
